// Logisim project SIN tp1.circ as structural Verilog
module \additioneur_à_1_bit  (
  input  in_1,
  input  in_2,
  input  in_3,
  output out_4,
  output out_5
);

  wire and_1_out, and_2_out, and_3_out, and_4_out, and_5_out, and_6_out, not_1_out, not_2_out, not_3_out,
       not_4_out, or_1_out;

  and and_1 (and_1_out, in_2, in_3);
  not not_1 (not_1_out, in_2);
  not not_2 (not_2_out, in_3);
  and and_2 (and_2_out, not_1_out, in_3);
  and and_3 (and_3_out, in_2, not_2_out);
  or or_1 (or_1_out, and_2_out, and_2_out, and_3_out, and_3_out);
  not not_3 (not_3_out, in_1);
  not not_4 (not_4_out, or_1_out);
  and and_4 (and_4_out, in_1, or_1_out);
  and and_5 (and_5_out, or_1_out, not_3_out);
  and and_6 (and_6_out, not_4_out, in_1);
  or or_2 (out_4, and_5_out, and_6_out);
  or or_3 (out_5, and_4_out, and_1_out);

  // Notes on the sheet:
  //   additioneur à 1 bit
endmodule

module \additioneur_à_3_bit  (
  input  in_1,
  input  in_2,
  input  in_3,
  input  in_4,
  input  in_5,
  input  in_6,
  input  in_7,
  output out_8,
  output out_9,
  output out_10,
  output out_11
);

  wire \additioneur_à_1_bit_1_out_5 , \additioneur_à_1_bit_2_out_5 ;

  \additioneur_à_1_bit  \additioneur_à_1_bit_1  (
    .in_1(in_1), .in_2(in_2), .in_3(in_3), .out_4(out_8), .out_5(\additioneur_à_1_bit_1_out_5 ));
  \additioneur_à_1_bit  \additioneur_à_1_bit_2  (
    .in_1(\additioneur_à_1_bit_1_out_5 ), .in_2(in_4), .in_3(in_5), .out_4(out_9),
    .out_5(\additioneur_à_1_bit_2_out_5 ));
  \additioneur_à_1_bit  \additioneur_à_1_bit_3  (
    .in_1(\additioneur_à_1_bit_2_out_5 ), .in_2(in_6), .in_3(in_7), .out_4(out_10), .out_5(out_11));
endmodule

module \ALU_à_1_bit  (
  input  in_1,
  input  in_2,
  input  in_3,
  input  in_4,
  input  in_5,
  input  in_6,
  input  in_7,
  input  in_8,
  output out_9,
  output out_10
);

  wire \additioneur_à_1_bit_1_out_4 , and_1_out, and_2_out, decoder_1_out_3, decoder_1_out_4,
       decoder_1_out_5, logical_unit_1_out_6, logical_unit_1_out_7, logical_unit_1_out_8,
       logical_unit_1_out_9, logical_unit_1_out_10, xor_1_out;

  and and_1 (and_1_out, in_3, in_4);
  and and_2 (and_2_out, in_5, in_6);
  xor xor_1 (xor_1_out, in_2, and_1_out);
  decoder decoder_1 (
    .in_1(in_7), .in_2(in_8), .out_3(decoder_1_out_3), .out_4(decoder_1_out_4), .out_5(decoder_1_out_5));  // open: out_6
  logical_unit logical_unit_1 (
    .in_1(xor_1_out), .in_2(and_2_out), .in_3(decoder_1_out_3), .in_4(decoder_1_out_4),
    .in_5(decoder_1_out_5), .out_6(logical_unit_1_out_6), .out_7(logical_unit_1_out_7),
    .out_8(logical_unit_1_out_8), .out_9(logical_unit_1_out_9), .out_10(logical_unit_1_out_10));
  \additioneur_à_1_bit  \additioneur_à_1_bit_1  (
    .in_1(in_1), .in_2(logical_unit_1_out_9), .in_3(logical_unit_1_out_10),
    .out_4(\additioneur_à_1_bit_1_out_4 ), .out_5(out_10));
  or or_1 (out_9, logical_unit_1_out_6, logical_unit_1_out_7, logical_unit_1_out_8, \additioneur_à_1_bit_1_out_4 );
endmodule

module logical_unit (
  input  in_1,
  input  in_2,
  input  in_3,
  input  in_4,
  input  in_5,
  output out_6,
  output out_7,
  output out_8,
  output out_9,
  output out_10
);

  wire and_1_out, not_1_out, or_1_out;

  not not_1 (not_1_out, in_2);
  and and_1 (and_1_out, in_1, in_2);
  or or_1 (or_1_out, in_1, in_2);
  and and_2 (out_6, and_1_out, in_3);
  and and_3 (out_7, or_1_out, in_4);
  and and_4 (out_8, not_1_out, in_5);

  assign out_9 = in_1;
  assign out_10 = in_2;
endmodule

module decoder (
  input  in_1,
  input  in_2,
  output out_3,
  output out_4,
  output out_5,
  output out_6
);

  wire not_1_out, not_2_out, not_3_out, not_4_out;

  not not_1 (not_1_out, in_1);
  not not_2 (not_2_out, in_2);
  not not_3 (not_3_out, in_1);
  not not_4 (not_4_out, in_2);
  and and_1 (out_3, not_1_out, not_2_out);
  and and_2 (out_4, in_2, not_3_out);
  and and_3 (out_5, in_1, not_4_out);
  and and_4 (out_6, in_1, in_2);
endmodule

module \ALU_à_3_bit  (
  input  in_1,
  input  in_2,
  input  in_3,
  input  in_4,
  input  in_5,
  input  in_6,
  input  in_7,
  input  in_8,
  input  in_9,
  input  in_10,
  input  in_11,
  input  in_12,
  output out_13,
  output out_14,
  output out_15,
  output out_16
);

  wire \alu_à_1_bit_1_out_10 , \alu_à_1_bit_2_out_10 ;

  \ALU_à_1_bit  \alu_à_1_bit_1  (
    .in_1(in_1), .in_2(in_2), .in_3(in_3), .in_4(in_4), .in_5(in_5), .in_6(in_6), .in_7(in_8), .in_8(in_7),
    .out_9(out_13), .out_10(\alu_à_1_bit_1_out_10 ));
  \ALU_à_1_bit  \alu_à_1_bit_2  (
    .in_1(\alu_à_1_bit_1_out_10 ), .in_2(in_8), .in_3(in_7), .in_4(in_6), .in_5(in_5), .in_6(in_4),
    .in_7(in_10), .in_8(in_9), .out_9(out_14), .out_10(\alu_à_1_bit_2_out_10 ));
  \ALU_à_1_bit  \alu_à_1_bit_3  (
    .in_1(\alu_à_1_bit_2_out_10 ), .in_2(in_4), .in_3(in_5), .in_4(in_6), .in_5(in_12), .in_6(in_7),
    .in_7(in_11), .in_8(in_8), .out_9(out_15), .out_10(out_16));
endmodule
